# Fritzing sketch Main_Task_1 (saved by Fritzing 0.9.3b)
circuit board: 8.46667cm x 5.64444cm
breadboards: 1

parts:
  Part1 = Arduino Uno (Rev3)
  920KV_Motor1 = DJI 920 KV Motor
  R1 = Rotary Potentiometer (Small) [maximum_resistance=100kΩ package=THT]
  Power_plug2 = Power plug
  M8 = ESC

nets:
  N1: Part1.A0, R1.wiper
  N2: Part1.D9_PWM, M8.DATA
  GND: Part1.GND, R1.leg1, M8.GND
  N3: Part1.5V, R1.leg2
  N4: 920KV_Motor1.w, M8.W
  N5: 920KV_Motor1.v, M8.V
  N6: 920KV_Motor1.u, M8.U
  N7: Power_plug2.GND, M8.GROUND
  VCC: Power_plug2.VCC, M8.VDD

notes:
  Brushless DC Motor
  Electronic Speed Controller
  Battery
  Potentiometer
  Arduino Uno

custom parts:
  DJI 920 KV Motor: DJI Brushless Outrunner 2212/920K Motor F330-550
